# Fritzing sketch board (saved by Fritzing 0.9.3b)
breadboards: 1

parts:
  U1 = NodeMCU V1.0
  DHT1 = DHT22 Humidity and Temperature Sensor
  Squix1 = OLED 0.96" 128x64 I2C SSD1306

nets:
  N1: U1.D3, Squix1.SCA
  N2: U1.D4, DHT1.DATA
  3V3: U1.3V3, DHT1.VDD, Squix1.VCC
  GND: U1.GND, DHT1.GND, Squix1.GND
  N3: U1.D5, Squix1.SCL

custom parts:
  NodeMCU V1.0: ESP8266 based NodeMCU
