# Fritzing sketch montage (saved by Fritzing 0.9.3b)
breadboards: 1

parts:
  U1 = NodeMCU V1.0
  R1 = Resistor [tolerance=±5% resistance=220 package=THT]
  DHT1 = DHT22 Humidity and Temperature Sensor

nets:
  N1: U1.D2, R1.Pin_0, DHT1.DATA
  3V3: U1.3V3, R1.Pin_1, DHT1.VDD
  GND: U1.GND, DHT1.GND

custom parts:
  NodeMCU V1.0: ESP8266 based NodeMCU
